// Logisim project RAM.circ as structural Verilog: 1 circuit, main circuit main
module main (
  input  in_1,
  input  in_2,
  input  in_3,
  input  in_4,
  input  in_5,
  input  in_6,
  input  in_7,
  input  in_8,
  input  in_9,
  output out_10,
  output out_11,
  output out_12,
  output out_13,
  output out_14,
  output out_15,
  output out_16,
  output out_17
);

  wire and_1_out, and_2_out, and_3_out, and_5_out, and_6_out, and_7_out, and_8_out, nand_1_out, not_1_out,
       not_2_out, not_3_out, not_4_out, not_5_out, or_1_out, or_2_out;

  nand nand_1 (nand_1_out, in_4, in_9);
  or or_1 (or_1_out, and_1_out, and_2_out);
  and and_1 (and_1_out, in_7, nand_1_out);
  nand nand_2 (out_10, in_2, out_11);
  nand nand_3 (out_11, out_10, in_1);
  nor nor_1 (out_12, in_1, out_13);
  nor nor_2 (out_13, out_12, in_2);
  and and_2 (and_2_out, or_1_out, not_1_out);
  not not_1 (not_1_out, nand_1_out);
  not not_2 (not_2_out, in_9);
  and and_3 (and_3_out, or_1_out, not_2_out);
  and and_4 (out_15, in_4, and_3_out);
  not not_3 (not_3_out, in_3);
  not not_4 (not_4_out, in_6);
  and and_5 (and_5_out, in_3, in_5);
  and and_6 (and_6_out, not_3_out, in_5);
  and and_7 (and_7_out, not_4_out, in_8);
  and and_8 (and_8_out, in_8, in_6);
  or or_2 (or_2_out, out_14, and_5_out);
  not not_5 (not_5_out, and_6_out);
  and and_9 (out_14, or_2_out, not_5_out);
  nor nor_3 (out_16, and_7_out, out_17);
  nor nor_4 (out_17, out_16, and_8_out);
endmodule
