// Logisim project Gates.circ as structural Verilog: 1 circuit, main circuit main
module main (
  input  in_1,
  input  in_2,
  input  in_3,
  input  in_4,
  input  in_5,
  input  in_6,
  input  NOR_Gate,
  input  in_8,
  input  NAND_Gate,
  input  in_10,
  input  in_11,
  input  in_12,
  output out_13,
  output out_14,
  output out_15,
  output out_16,
  output out_17,
  output out_18
);

  wire and_1_out, nand_1_out, nand_2_out, nand_3_out, or_1_out, transistor_1_out, transistor_5_out;

  Transistor #(.\type ("n")) transistor_1 (.in(in_5), .out(transistor_1_out), .gate(in_4));
  Transistor #(.\type ("n"), .gate("br")) transistor_2 (.in(in_5), .out(out_15), .gate(in_6));
  and and_1 (and_1_out, NAND_Gate, in_11);
  Transistor transistor_3 (.in(1'b1), .out(out_13), .gate(in_1));
  Transistor #(.\type ("n")) transistor_4 (.in(transistor_5_out), .out(out_14), .gate(in_3));
  Transistor #(.\type ("n")) transistor_5 (.in(1'b1), .out(transistor_5_out), .gate(in_2));
  not not_1 (out_17, and_1_out);
  Pull_Resistor pull_resistor_1 (.node(out_13));
  not not_2 (out_16, or_1_out);
  or or_1 (or_1_out, NOR_Gate, in_8);
  nand nand_1 (nand_1_out, in_10, in_12);
  nand nand_2 (nand_2_out, in_10, nand_1_out);
  nand nand_3 (nand_3_out, nand_1_out, in_12);
  nand nand_4 (out_18, nand_2_out, nand_3_out);

  // Notes on the sheet:
  //   OR
  //   AND Gate
  //   NOT Gate
  //   XOR
endmodule
