// Logisim project WhatGameToPlay.circ as structural Verilog: 1 circuit, main circuit main
module main (
  input  Feling_fast,
  input  in_2,
  input  Want_to_fly,
  input  At_DigiPen,
  input  in_5,
  output None,
  output MC,
  output RL
);

  wire and_1_out, and_2_out, and_3_out, and_4_out, and_5_out, and_6_out, and_7_out, and_8_out, and_10_out,
       not_1_out, not_2_out, not_3_out, not_4_out, not_5_out, not_6_out;

  and and_1 (and_1_out, in_2, Want_to_fly);
  not not_1 (not_1_out, At_DigiPen);
  not not_2 (not_2_out, At_DigiPen);
  and and_2 (and_2_out, At_DigiPen, Want_to_fly, in_5);
  and and_3 (and_3_out, in_2, At_DigiPen, in_5);
  buf and_4 (and_4_out, and_1_out);  // AND_Gate
  and and_5 (and_5_out, Feling_fast, Want_to_fly, in_2, not_1_out, not_2_out);
  not not_3 (not_3_out, and_3_out);
  and and_6 (and_6_out, not_3_out, Want_to_fly, Feling_fast);
  and and_7 (and_7_out, and_4_out, At_DigiPen);
  not not_4 (not_4_out, RL);
  or or_1 (MC, and_7_out, and_2_out);
  and and_8 (and_8_out, and_6_out, not_4_out);
  and and_9 (RL, and_6_out, and_5_out);
  not not_5 (not_5_out, MC);
  not not_6 (not_6_out, RL);
  or or_2 (None, and_8_out, and_10_out);
  and and_10 (and_10_out, not_5_out, not_6_out);

  // Notes on the sheet:
  //   Have a controller?
  //   Have a mouse?
  //   What game do I want to play?
endmodule
