// Logisim project WhatGameToPlay.circ as structural Verilog: 1 circuit, main circuit main
module main (
  input  in_1,
  input  At_DigiPen,
  input  Have_a_mouse,
  input  in_4,
  input  Feling_fast,
  input  in_6,
  input  Want_to_fly,
  input  At_DigiPen_2,
  input  in_9,
  input  in_10,
  input  At_DigiPen_3,
  input  Have_a_mouse_2,
  input  in_13,
  output None,
  output MC,
  output RL,
  output None_2,
  output MC_2,
  output RL_2,
  output None_3,
  output MC_3,
  output RL_3
);

  wire and_1_out, and_3_out, and_4_out, and_5_out, and_6_out, and_7_out, and_8_out, and_9_out, and_10_out,
       and_11_out, and_12_out, and_13_out, and_14_out, and_15_out, and_16_out, and_20_out, and_21_out,
       not_1_out, not_2_out, not_3_out, not_4_out, not_5_out, not_6_out, not_7_out, not_8_out, not_9_out,
       not_10_out, not_11_out, not_12_out, not_13_out, not_14_out, not_15_out, not_16_out, not_17_out,
       not_18_out, not_19_out, not_20_out, not_21_out, not_22_out, not_23_out, or_2_out;

  not not_1 (not_1_out, Have_a_mouse);
  not not_2 (not_2_out, in_4);
  not not_3 (not_3_out, At_DigiPen);
  not not_4 (not_4_out, Have_a_mouse);
  not not_5 (not_5_out, in_4);
  not not_6 (not_6_out, in_1);
  not not_7 (not_7_out, Have_a_mouse);
  and and_1 (and_1_out, in_1, At_DigiPen, Have_a_mouse);
  not not_8 (not_8_out, At_DigiPen);
  and and_2 (RL, in_1, not_8_out, in_4);
  and and_3 (and_3_out, in_6, not_9_out);
  not not_9 (not_9_out, Want_to_fly);
  not not_10 (not_10_out, At_DigiPen_2);
  and and_4 (and_4_out, in_1, At_DigiPen, not_1_out, not_2_out);
  and and_5 (and_5_out, in_1, not_3_out, not_4_out, not_5_out);
  and and_6 (and_6_out, in_1, At_DigiPen, not_7_out, in_4);
  not not_11 (not_11_out, At_DigiPen_2);
  and and_7 (and_7_out, At_DigiPen_2, Want_to_fly, in_9);
  not not_12 (not_12_out, At_DigiPen_3);
  not not_13 (not_13_out, At_DigiPen);
  and and_8 (and_8_out, in_1, not_13_out, not_14_out, not_15_out);
  not not_14 (not_14_out, not_7_out);
  not not_15 (not_15_out, in_4);
  not not_16 (not_16_out, and_9_out);
  and and_9 (and_9_out, in_6, At_DigiPen_2, in_9);
  buf and_10 (and_10_out, and_3_out);  // AND_Gate
  and and_11 (and_11_out, Feling_fast, not_9_out, in_6, not_10_out, not_11_out);
  and and_12 (and_12_out, in_10, At_DigiPen_3, Have_a_mouse_2);
  and and_13 (and_13_out, in_13, in_10, not_12_out);
  and and_14 (and_14_out, not_16_out, not_9_out, Feling_fast);
  or or_1 (MC_2, and_15_out, and_7_out);
  and and_15 (and_15_out, and_10_out, At_DigiPen_2);
  not not_17 (not_17_out, RL_2);
  not not_18 (not_18_out, At_DigiPen_3);
  or or_2 (or_2_out, and_12_out, and_13_out);
  or or_3 (None, and_4_out, and_5_out, not_6_out, and_6_out);
  or or_4 (MC, and_8_out, and_1_out);
  and and_16 (and_16_out, and_14_out, not_17_out);
  and and_17 (RL_2, and_14_out, and_11_out);
  not not_19 (not_19_out, in_10);
  and and_18 (RL_3, not_18_out, or_2_out);
  or or_5 (None_2, and_16_out, and_20_out);
  not not_20 (not_20_out, MC_2);
  not not_21 (not_21_out, RL_2);
  and and_19 (None_3, not_19_out, and_21_out);
  buf or_6 (MC_3, RL_3);  // OR_Gate
  Controlled_Inverter controlled_inverter_1 ();  // open: in, out, en
  and and_20 (and_20_out, not_20_out, not_21_out);
  not not_22 (not_22_out, MC_3);
  not not_23 (not_23_out, RL_3);
  and and_21 (and_21_out, not_22_out, not_23_out);

  // Notes on the sheet:
  //   Want to Play a game?
  //   What game do I want to play?
  //   Have a controller?
  //   Mess up #1
  //   Have a controller?
  //   Have a mouse?
  //   Mess up #2
  //   Want to Play a game?
  //   Have a controller?
endmodule
